# Fritzing sketch Circuit (saved by Fritzing 0.8.7b)
breadboards: 1

parts:
  U1 = 3.5mm Audio Jack [package=audio-jack-3.5mm-smd]
  Part1 = Arduino Uno (Rev3)
  VCC1 = Battery
  IC1 = L293D [package=THT]
  M1 = DC Motor
  M2 = DC Motor

nets:
  N1: U1.RIGHT, Part1.A0
  N2: U1.SLEEVE, Part1.GND, VCC1.-, IC1.0V
  N3: Part1.D8, IC1.In_4
  N4: Part1.D9_PWM, IC1.In_3
  N5: Part1.D6_PWM, IC1.In_1
  N6: Part1.D7, IC1.In_2
  N7: Part1.5V, IC1.Enable_1, IC1.+Vmotor, IC1.Enable_2, IC1.+V
  N8: Part1.VIN, VCC1.+
  N9: IC1.Out_1_(_Controlled_by_Enable_1_), M1.pin_2
  N10: IC1.Out_2_(_Controlled_by_Enable_1_), M1.pin_1
  N11: IC1.Out_3_(_Controlled_by_Enable_2_), M2.pin_1
  N12: IC1.Out_4_(_Controlled_by_Enable_2_), M2.pin_2

notes:
  iPhone
